// Logisim project cpu.circ as structural Verilog: 9 circuits, main circuit ALU
module ALU (
  input  [31:0] A,
  input  [31:0] B,
  input  [3:0] ALUSel,
  output [31:0] out_4
);

  wire comparator_1_lt;
  wire [4:0] bit_extender_1_out, bit_extender_2_out, bit_extender_4_out;
  wire [31:0] add, and1, mul, mulh, mulhu, or1, sll1, slt, sra1, srl1, sub, xor1;

  Bit_Extender #(.in_width(32), .out_width(5)) bit_extender_1 (.in(B), .out(bit_extender_1_out));
  Comparator #(.width(32)) comparator_1 (.a(A), .b(B), .lt(comparator_1_lt));  // open: gt, eq
  Bit_Extender #(.in_width(32), .out_width(5)) bit_extender_2 (.in(B), .out(bit_extender_2_out));
  Adder #(.width(32)) adder_1 (.a(A), .b(B), .out(add));  // open: cin, cout
  Shifter #(.width(32)) shifter_1 (.in(A), .\dist (bit_extender_1_out), .out(sll1));
  assign slt = {{31{comparator_1_lt}}, comparator_1_lt};  // Bit_Extender bit_extender_3
  assign xor1 = A ^ B;  // XOR_Gate xor_1, 32 bits wide
  Shifter #(.shift("lr"), .width(32)) shifter_2 (.in(A), .\dist (bit_extender_2_out), .out(srl1));
  assign or1 = A | B;  // OR_Gate or_1, 32 bits wide
  assign and1 = A & B;  // AND_Gate and_1, 32 bits wide
  Multiplier #(.mode("twosComplement"), .width(32)) multiplier_1 (.a(A), .b(B), .out(mul));  // open: cin, cout
  Multiplier #(.mode("twosComplement"), .width(32)) multiplier_2 (.a(A), .b(B), .out(mulh));  // open: cin, cout
  Multiplier #(.width(32)) multiplier_3 (.a(A), .b(B), .out(mulhu));  // open: cin, cout
  Subtractor #(.width(32)) subtractor_1 (.a(A), .b(B), .out(sub));  // open: bin, bout
  Bit_Extender #(.in_width(32), .out_width(5)) bit_extender_4 (.in(B), .out(bit_extender_4_out));
  Shifter #(.shift("ar"), .width(32)) shifter_3 (.in(A), .\dist (bit_extender_4_out), .out(sra1));
  Multiplexer #(.select(4), .width(32)) multiplexer_1 (
    .in0(add), .in1(sll1), .in2(slt), .in4(xor1), .in5(srl1), .in6(or1), .in7(and1), .in8(mul), .in9(mulh),
    .in11(mulhu), .in12(sub), .in13(sra1), .in15(B), .out(out_4), .sel(ALUSel));  // open: in3, in10, in14
endmodule

module cpu (
  input  [31:0] READ_DATA,
  input  [31:0] INSTRUCTION,
  input  in_3,
  output [31:0] WRITE_ADDRESS,
  output [31:0] PROGRAM_COUNTER,
  output [31:0] WRITE_DATA,
  output [31:0] ra,
  output [31:0] sp,
  output [31:0] t0,
  output [31:0] t1,
  output [31:0] t2,
  output [31:0] s0,
  output [31:0] s1,
  output [31:0] a0,
  output WRITE_ENABLE
);

  wire Asel, BrEq, BrLt, BrUn, Bsel, flush, PCsel, RegWen;
  wire [1:0] WBsel;
  wire [2:0] immsel;
  wire [3:0] ALUsel;
  wire [31:0] adder_1_out, adder_2_out, immgen_1_imm, multiplexer_1_out, multiplexer_2_out,
       multiplexer_3_out, multiplexer_4_out, multiplexer_5_out, regfile_1_rdata1, register_1_q, register_2_q;

  Register #(.width(32)) pc (.D(multiplexer_1_out), .clk(in_3), .Q(PROGRAM_COUNTER));  // open: en, clr
  Multiplexer #(.width(32)) multiplexer_1 (
    .in0(adder_1_out), .in1(WRITE_ADDRESS), .out(multiplexer_1_out), .sel(PCsel));
  Adder #(.width(32)) adder_1 (.a(32'h4), .b(PROGRAM_COUNTER), .out(adder_1_out));  // open: cin, cout
  Register #(.width(32)) register_1 (.D(PROGRAM_COUNTER), .clk(in_3), .Q(register_1_q));  // open: en, clr
  Register #(.width(32)) register_2 (.D(multiplexer_2_out), .clk(in_3), .Q(register_2_q));  // open: en, clr
  Multiplexer #(.width(32)) multiplexer_2 (.in0(INSTRUCTION), .in1(32'h33), .out(multiplexer_2_out), .sel(flush));
  // controller controller_1: pin names not known; wires that end beside it: register_2_q, BrEq, BrLt, ALUsel, BrUn, flush, Asel, PCsel, Bsel, WBsel, RegWen, WRITE_ENABLE, immsel
  RegFile regfile_1 (
    .wb(multiplexer_5_out), .clock(in_3), .rd(register_2_q[11:7]), .RegWen(RegWen),
    .rs1(register_2_q[19:15]), .rs2(register_2_q[24:20]), .Rdata1(regfile_1_rdata1), .Rdata2(WRITE_DATA),
    .ra(ra), .sp(sp), .t0(t0), .t1(t1), .t2(t2), .s0(s0), .s1(s1), .a0(a0));
  immgen immgen_1 (.inst(register_2_q), .immsel(immsel), .imm(immgen_1_imm));  // open: out_4
  branchcomp branchcomp_1 (.rs1(regfile_1_rdata1), .rs2(WRITE_DATA), .BrUn(BrUn), .BrEq(BrEq), .BrLt(BrLt));
  Multiplexer #(.width(32)) multiplexer_3 (.in0(WRITE_DATA), .in1(immgen_1_imm), .out(multiplexer_3_out), .sel(Bsel));
  Multiplexer #(.width(32)) multiplexer_4 (
    .in0(regfile_1_rdata1), .in1(register_1_q), .out(multiplexer_4_out), .sel(Asel));
  ALU alu_1 (.A(multiplexer_4_out), .B(multiplexer_3_out), .ALUSel(ALUsel), .out_4(WRITE_ADDRESS));
  Adder #(.width(32)) adder_2 (.a(32'h4), .b(register_1_q), .out(adder_2_out));  // open: cin, cout
  Multiplexer #(.select(2), .width(32)) multiplexer_5 (
    .in0(READ_DATA), .in1(WRITE_ADDRESS), .in2(adder_2_out), .out(multiplexer_5_out), .sel(WBsel));  // open: in3

  // Other names for the same wires on the sheet: clock = in_3
endmodule

module RegFile (
  input  [31:0] wb,
  input  clock,
  input  [4:0] rd,
  input  RegWen,
  input  [4:0] rs1,
  input  [4:0] rs2,
  output [31:0] Rdata1,
  output [31:0] Rdata2,
  output [31:0] ra,
  output [31:0] sp,
  output [31:0] t0,
  output [31:0] t1,
  output [31:0] t2,
  output [31:0] s0,
  output [31:0] s1,
  output [31:0] a0
);

  wire [31:0] demultiplexer_1_out1, demultiplexer_1_out2, demultiplexer_1_out5, demultiplexer_1_out6,
       demultiplexer_1_out7, demultiplexer_1_out8, demultiplexer_1_out9, demultiplexer_1_out10,
       regplexer_1_out_5, regplexer_2_out_5, regplexer_3_out_5, regplexer_4_out_5, regplexer_5_out_5,
       regplexer_6_out_5, regplexer_7_out_5, regplexer_8_out_5;

  Demultiplexer #(.select(5), .width(32)) demultiplexer_1 (
    .out1(demultiplexer_1_out1), .out2(demultiplexer_1_out2), .out5(demultiplexer_1_out5),
    .out6(demultiplexer_1_out6), .out7(demultiplexer_1_out7), .out8(demultiplexer_1_out8),
    .out9(demultiplexer_1_out9), .out10(demultiplexer_1_out10), .in(wb), .sel(rd));  // open: out0, out3, out4, out11, out12, out13, out14, out15, out16, out17, out18, out19, out20, out21, out22, out23, out24, out25, out26, out27, out28, out29, out30, out31
  regplexer regplexer_1 (
    .index(5'b00001), .rdsel(rd), .self(ra), .write(demultiplexer_1_out1), .out_5(regplexer_1_out_5));
  Register #(.width(32)) RegRA (.D(regplexer_1_out_5), .en(RegWen), .clk(clock), .Q(ra));  // open: clr
  regplexer regplexer_2 (
    .index(5'b00010), .rdsel(rd), .self(sp), .write(demultiplexer_1_out2), .out_5(regplexer_2_out_5));
  Register #(.width(32)) RegSP (.D(regplexer_2_out_5), .en(RegWen), .clk(clock), .Q(sp));  // open: clr
  regplexer regplexer_3 (
    .index(5'b00101), .rdsel(rd), .self(t0), .write(demultiplexer_1_out5), .out_5(regplexer_3_out_5));
  Register #(.width(32)) RegT0 (.D(regplexer_3_out_5), .en(RegWen), .clk(clock), .Q(t0));  // open: clr
  regplexer regplexer_4 (
    .index(5'b00110), .rdsel(rd), .self(t1), .write(demultiplexer_1_out6), .out_5(regplexer_4_out_5));
  Register #(.width(32)) RegT1 (.D(regplexer_4_out_5), .en(RegWen), .clk(clock), .Q(t1));  // open: clr
  Multiplexer #(.select(5), .width(32)) multiplexer_1 (
    .in0({32{1'b0}}), .in1(ra), .in2(sp), .in5(t0), .in6(t1), .in7(t2), .in8(s0), .in9(s1), .in10(a0),
    .out(Rdata1), .sel(rs1));  // open: in3, in4, in11, in12, in13, in14, in15, in16, in17, in18, in19, in20, in21, in22, in23, in24, in25, in26, in27, in28, in29, in30, in31
  Multiplexer #(.select(5), .width(32)) multiplexer_2 (
    .in0({32{1'b0}}), .in1(ra), .in2(sp), .in5(t0), .in6(t1), .in7(t2), .in8(s0), .in9(s1), .in10(a0),
    .out(Rdata2), .sel(rs2));  // open: in3, in4, in11, in12, in13, in14, in15, in16, in17, in18, in19, in20, in21, in22, in23, in24, in25, in26, in27, in28, in29, in30, in31
  regplexer regplexer_5 (
    .index(5'b00111), .rdsel(rd), .self(t2), .write(demultiplexer_1_out7), .out_5(regplexer_5_out_5));
  Register #(.width(32)) RegT2 (.D(regplexer_5_out_5), .en(RegWen), .clk(clock), .Q(t2));  // open: clr
  regplexer regplexer_6 (
    .index(5'b01000), .rdsel(rd), .self(s0), .write(demultiplexer_1_out8), .out_5(regplexer_6_out_5));
  Register #(.width(32)) RegS0 (.D(regplexer_6_out_5), .en(RegWen), .clk(clock), .Q(s0));  // open: clr
  regplexer regplexer_7 (
    .index(5'b01001), .rdsel(rd), .self(s1), .write(demultiplexer_1_out9), .out_5(regplexer_7_out_5));
  Register #(.width(32)) RegS1 (.D(regplexer_7_out_5), .en(RegWen), .clk(clock), .Q(s1));  // open: clr
  regplexer regplexer_8 (
    .index(5'b01010), .rdsel(rd), .self(a0), .write(demultiplexer_1_out10), .out_5(regplexer_8_out_5));
  Register #(.width(32)) RegA0 (.D(regplexer_8_out_5), .en(RegWen), .clk(clock), .Q(a0));  // open: clr
endmodule

module TEST (
  input  [31:0] in_1,
  input  [31:0] in_2,
  input  [3:0] in_3,
  input  [31:0] in_4,
  input  [31:0] in_5,
  input  [31:0] in_6,
  input  [4:0] in_7,
  input  in_8,
  input  [4:0] in_9,
  input  [4:0] in_10,
  output [31:0] out_11,
  output [31:0] out_12,
  output [31:0] out_13,
  output [31:0] out_14,
  output [31:0] out_15,
  output [31:0] out_16,
  output [31:0] out_17,
  output [31:0] out_18,
  output [31:0] out_19,
  output [31:0] out_20,
  output [31:0] out_21,
  output [31:0] out_22,
  output out_23,
  output [31:0] out_24,
  output [31:0] out_25,
  output [31:0] out_26,
  output [31:0] out_27,
  output [31:0] out_28,
  output [31:0] out_29,
  output [31:0] out_30,
  output [31:0] out_31,
  output [31:0] out_32,
  output [31:0] out_33
);

  wire clock_1_out, clock_2_out;

  Clock clock_1 (.out(clock_1_out));
  Clock clock_2 (.out(clock_2_out));
  ALU alu_1 (.A(in_1), .B(in_2), .ALUSel(in_3), .out_4(out_11));
  cpu cpu_1 (
    .READ_DATA(in_4), .INSTRUCTION(in_5), .in_3(clock_1_out), .WRITE_ADDRESS(out_12),
    .PROGRAM_COUNTER(out_13), .WRITE_DATA(out_14), .ra(out_15), .sp(out_16), .t0(out_17), .t1(out_18),
    .t2(out_19), .s0(out_20), .s1(out_21), .a0(out_22), .WRITE_ENABLE(out_23));
  RegFile regfile_1 (
    .wb(in_6), .clock(clock_2_out), .rd(in_7), .RegWen(in_8), .rs1(in_9), .rs2(in_10), .Rdata1(out_24),
    .Rdata2(out_25), .ra(out_26), .sp(out_27), .t0(out_28), .t1(out_29), .t2(out_30), .s0(out_31),
    .s1(out_32), .a0(out_33));
endmodule

module regplexer (
  input  [31:0] self,
  input  [31:0] write,
  input  [4:0] index,
  input  [4:0] rdsel,
  output [31:0] out_5
);

  wire comparator_1_eq;

  Comparator #(.width(5)) comparator_1 (.a(index), .b(rdsel), .eq(comparator_1_eq));  // open: gt, lt
  Multiplexer #(.width(32)) multiplexer_1 (.in0(self), .in1(write), .out(out_5), .sel(comparator_1_eq));
endmodule

module immgen (
  input  [31:0] inst,
  input  [2:0] immsel,
  output [31:0] imm,
  output [31:0] out_4
);

  wire [31:0] bit_extender_1_out, bit_extender_2_out, bit_extender_3_out, bit_extender_4_out;

  assign bit_extender_1_out = {{20{1'b0}}, inst[31:20]};  // Bit_Extender bit_extender_1
  assign bit_extender_2_out = {{20{1'b0}}, {inst[31:25], inst[11:7]}};  // Bit_Extender bit_extender_2
  assign bit_extender_3_out = {{19{1'b0}}, {inst[31], inst[7], inst[30:25], inst[11:8], 1'b0}};  // Bit_Extender bit_extender_3
  assign bit_extender_4_out = {{11{1'b0}}, {inst[31], inst[19:12], inst[20], inst[30:21], 1'b0}};  // Bit_Extender bit_extender_4
  Multiplexer #(.select(3), .width(32)) multiplexer_1 (
    .in1(bit_extender_1_out), .in2(bit_extender_2_out), .in3(bit_extender_3_out),
    .in4({inst[31:12], {12{1'b0}}}), .in5(bit_extender_4_out), .out(imm), .sel(immsel));  // open: in0, in6, in7

  assign out_4 = {inst[31:12], {12{1'b0}}};

  // Notes on the sheet:
  //   inst: initial=0xffffffff
endmodule

module controller (
  input  [31:0] instruction,
  input  BrEq,
  input  BrLt,
  output [3:0] ALUsel,
  output Brun,
  output flush,
  output Asel,
  output MemRw,
  output RegWen,
  output PCsel,
  output [1:0] WBsel,
  output [2:0] IMMsel,
  output Bsel
);

  wire add, addi, and1, and_1_out, and_2_out, and_3_out, and_4_out, and_5_out, and_6_out, andi, auipc, beq,
       bge, bgeu, blt, bltu, bne, comparator_10_eq, comparator_11_eq, comparator_12_eq, comparator_13_eq,
       comparator_14_eq, comparator_15_eq, comparator_16_eq, comparator_17_eq, comparator_18_eq,
       comparator_19_eq, comparator_20_eq, comparator_21_eq, comparator_22_eq, comparator_23_eq,
       comparator_24_eq, comparator_25_eq, comparator_26_eq, comparator_27_eq, comparator_28_eq,
       comparator_29_eq, comparator_30_eq, comparator_31_eq, comparator_32_eq, comparator_33_eq,
       comparator_34_eq, comparator_35_eq, comparator_36_eq, comparator_37_eq, comparator_38_eq,
       comparator_39_eq, comparator_40_eq, comparator_41_eq, comparator_42_eq, comparator_43_eq,
       comparator_44_eq, comparator_45_eq, comparator_46_eq, comparator_47_eq, comparator_48_eq,
       comparator_49_eq, comparator_50_eq, comparator_51_eq, comparator_52_eq, comparator_53_eq,
       comparator_54_eq, comparator_55_eq, comparator_56_eq, Itypeload, Itypeother, jal, jalr, lb, lh, lui,
       lw, mul, mulh, mulhu, not_1_out, not_2_out, not_3_out, or1, or_1_out, or_2_out, or_3_out, or_4_out,
       or_6_out, or_8_out, or_10_out, or_11_out, or_13_out, or_15_out, ori, Rtype, sb, SBtype, sh, sll1,
       slli, slt, slti, sra1, srai, srl1, srli, Stype, sub, sw, xor1, xori;
  wire [1:0] multiplexer_1_out, multiplexer_2_out, or_12_out;
  wire [2:0] multiplexer_4_out, multiplexer_5_out, multiplexer_6_out, multiplexer_7_out, multiplexer_8_out,
       or_17_out;
  wire [3:0] multiplexer_9_out, multiplexer_10_out, multiplexer_11_out, multiplexer_12_out,
       multiplexer_13_out, multiplexer_14_out, multiplexer_15_out, multiplexer_16_out, multiplexer_17_out,
       multiplexer_18_out, multiplexer_19_out, multiplexer_20_out, multiplexer_21_out, multiplexer_22_out,
       multiplexer_23_out, multiplexer_24_out, multiplexer_25_out, multiplexer_26_out, multiplexer_27_out,
       multiplexer_28_out, multiplexer_29_out, multiplexer_30_out, multiplexer_31_out, multiplexer_32_out,
       multiplexer_33_out, multiplexer_34_out, multiplexer_35_out, multiplexer_36_out, multiplexer_37_out,
       multiplexer_38_out, multiplexer_39_out, multiplexer_40_out, multiplexer_41_out, multiplexer_42_out,
       or_19_out, or_20_out, or_21_out, or_22_out, or_23_out, or_24_out, or_25_out, or_26_out, or_27_out,
       or_28_out, or_29_out, or_30_out, or_31_out, or_32_out, or_33_out, or_34_out, or_35_out, or_36_out,
       or_37_out, or_38_out, or_39_out, or_40_out, or_41_out, or_42_out, or_43_out, or_44_out, or_45_out,
       or_46_out;

  not not_1 (not_1_out, BrEq);
  not not_2 (not_2_out, BrLt);
  not not_3 (not_3_out, BrLt);
  Comparator #(.width(7)) comparator_1 (.a(7'b0110011), .b(instruction[6:0]), .eq(Rtype));  // open: gt, lt
  Comparator #(.width(7)) comparator_2 (.a(7'b0000011), .b(instruction[6:0]), .eq(Itypeload));  // open: gt, lt
  Comparator #(.width(7)) comparator_3 (.a(7'b0010011), .b(instruction[6:0]), .eq(Itypeother));  // open: gt, lt
  Comparator #(.width(7)) comparator_4 (.a(7'b0100011), .b(instruction[6:0]), .eq(Stype));  // open: gt, lt
  Comparator #(.width(7)) comparator_5 (.a(7'b1100011), .b(instruction[6:0]), .eq(SBtype));  // open: gt, lt
  Comparator #(.width(7)) comparator_6 (.a(7'b0010111), .b(instruction[6:0]), .eq(auipc));  // open: gt, lt
  Comparator #(.width(7)) comparator_7 (.a(7'b0110111), .b(instruction[6:0]), .eq(lui));  // open: gt, lt
  Comparator #(.width(7)) comparator_8 (.a(7'b1100111), .b(instruction[6:0]), .eq(jalr));  // open: gt, lt
  Comparator #(.width(7)) comparator_9 (.a(7'b1101111), .b(instruction[6:0]), .eq(jal));  // open: gt, lt
  and and_1 (and_1_out, BrEq, beq);
  and and_2 (and_2_out, bne, not_1_out);
  and and_3 (and_3_out, blt, BrLt);
  and and_4 (and_4_out, bge, not_2_out);
  and and_5 (and_5_out, bltu, BrLt);
  and and_6 (and_6_out, bgeu, not_3_out);
  or or_1 (or_1_out, and_1_out, and_2_out);
  or or_2 (or_2_out, and_3_out, and_4_out);
  or or_3 (or_3_out, and_5_out, and_6_out);
  or or_4 (or_4_out, or_1_out, or_2_out, or_3_out, jal);
  or or_5 (Bsel, 1'b0, or_6_out);
  or or_6 (or_6_out, Stype, Itypeload, Itypeother, SBtype, auipc, lui, jal, jalr);
  Comparator #(.width(7)) comparator_10 (.a({7{1'b0}}), .b(instruction[31:25]), .eq(comparator_10_eq));  // open: gt, lt
  Comparator #(.width(3)) comparator_11 (.a(3'b000), .b(instruction[14:12]), .eq(comparator_11_eq));  // open: gt, lt
  Comparator #(.width(7)) comparator_12 (
    .a(7'b0000001), .b(instruction[31:25]), .eq(comparator_12_eq));  // open: gt, lt
  Comparator #(.width(3)) comparator_13 (.a(3'b000), .b(instruction[14:12]), .eq(comparator_13_eq));  // open: gt, lt
  Comparator #(.width(7)) comparator_14 (
    .a(7'b0100000), .b(instruction[31:25]), .eq(comparator_14_eq));  // open: gt, lt
  Comparator #(.width(3)) comparator_15 (.a(3'b000), .b(instruction[14:12]), .eq(comparator_15_eq));  // open: gt, lt
  Comparator #(.width(7)) comparator_16 (.a({7{1'b0}}), .b(instruction[31:25]), .eq(comparator_16_eq));  // open: gt, lt
  Comparator #(.width(3)) comparator_17 (.a(3'b001), .b(instruction[14:12]), .eq(comparator_17_eq));  // open: gt, lt
  Comparator #(.width(7)) comparator_18 (
    .a(7'b0000001), .b(instruction[31:25]), .eq(comparator_18_eq));  // open: gt, lt
  Comparator #(.width(3)) comparator_19 (.a(3'b001), .b(instruction[14:12]), .eq(comparator_19_eq));  // open: gt, lt
  Comparator #(.width(7)) comparator_20 (
    .a(7'b0000001), .b(instruction[31:25]), .eq(comparator_20_eq));  // open: gt, lt
  Comparator #(.width(3)) comparator_21 (.a(3'b011), .b(instruction[14:12]), .eq(comparator_21_eq));  // open: gt, lt
  Comparator #(.width(3)) comparator_22 (.a(3'b000), .b(instruction[14:12]), .eq(comparator_22_eq));  // open: gt, lt
  Comparator #(.width(3)) comparator_23 (.a(3'b001), .b(instruction[14:12]), .eq(comparator_23_eq));  // open: gt, lt
  Comparator #(.width(3)) comparator_24 (.a(3'b010), .b(instruction[14:12]), .eq(comparator_24_eq));  // open: gt, lt
  or or_7 (Asel, 1'b0, or_4_out);
  or or_8 (or_8_out, or_4_out, jalr);
  and and_7 (add, comparator_10_eq, comparator_11_eq, Rtype);
  and and_8 (mul, comparator_12_eq, comparator_13_eq, Rtype);
  and and_9 (sub, comparator_14_eq, comparator_15_eq, Rtype);
  and and_10 (sll1, comparator_16_eq, comparator_17_eq, Rtype);
  and and_11 (mulh, comparator_18_eq, comparator_19_eq, Rtype);
  and and_12 (mulhu, comparator_20_eq, comparator_21_eq, Rtype);
  and and_13 (sb, comparator_22_eq, Stype);
  and and_14 (sh, comparator_23_eq, Stype);
  and and_15 (sw, comparator_24_eq, Stype);
  or or_9 (flush, or_8_out, 1'b0);
  Comparator #(.width(7)) comparator_25 (.a({7{1'b0}}), .b(instruction[31:25]), .eq(comparator_25_eq));  // open: gt, lt
  Comparator #(.width(3)) comparator_26 (.a(3'b010), .b(instruction[14:12]), .eq(comparator_26_eq));  // open: gt, lt
  Comparator #(.width(7)) comparator_27 (.a({7{1'b0}}), .b(instruction[31:25]), .eq(comparator_27_eq));  // open: gt, lt
  Comparator #(.width(3)) comparator_28 (.a(3'b100), .b(instruction[14:12]), .eq(comparator_28_eq));  // open: gt, lt
  Comparator #(.width(7)) comparator_29 (.a({7{1'b0}}), .b(instruction[31:25]), .eq(comparator_29_eq));  // open: gt, lt
  Comparator #(.width(3)) comparator_30 (.a(3'b101), .b(instruction[14:12]), .eq(comparator_30_eq));  // open: gt, lt
  Comparator #(.width(7)) comparator_31 (
    .a(7'b0100000), .b(instruction[31:25]), .eq(comparator_31_eq));  // open: gt, lt
  Comparator #(.width(3)) comparator_32 (.a(3'b101), .b(instruction[14:12]), .eq(comparator_32_eq));  // open: gt, lt
  Comparator #(.width(7)) comparator_33 (.a({7{1'b0}}), .b(instruction[31:25]), .eq(comparator_33_eq));  // open: gt, lt
  Comparator #(.width(3)) comparator_34 (.a(3'b110), .b(instruction[14:12]), .eq(comparator_34_eq));  // open: gt, lt
  Comparator #(.width(7)) comparator_35 (.a({7{1'b0}}), .b(instruction[31:25]), .eq(comparator_35_eq));  // open: gt, lt
  Comparator #(.width(3)) comparator_36 (.a(3'b111), .b(instruction[14:12]), .eq(comparator_36_eq));  // open: gt, lt
  Comparator #(.width(3)) comparator_37 (.a(3'b000), .b(instruction[14:12]), .eq(comparator_37_eq));  // open: gt, lt
  Comparator #(.width(3)) comparator_38 (.a(3'b001), .b(instruction[14:12]), .eq(comparator_38_eq));  // open: gt, lt
  Comparator #(.width(3)) comparator_39 (.a(3'b100), .b(instruction[14:12]), .eq(comparator_39_eq));  // open: gt, lt
  and and_16 (slt, comparator_25_eq, comparator_26_eq, Rtype);
  and and_17 (xor1, comparator_27_eq, comparator_28_eq, Rtype);
  and and_18 (srl1, comparator_29_eq, comparator_30_eq, Rtype);
  and and_19 (sra1, comparator_31_eq, comparator_32_eq, Rtype);
  and and_20 (or1, comparator_33_eq, comparator_34_eq, Rtype);
  and and_21 (and1, comparator_35_eq, comparator_36_eq, Rtype);
  and and_22 (beq, comparator_37_eq, SBtype);
  and and_23 (bne, comparator_38_eq, SBtype);
  and and_24 (blt, comparator_39_eq, SBtype);
  Multiplexer #(.width(2)) multiplexer_1 (.in0(2'b00), .in1(2'b01), .out(multiplexer_1_out), .sel(Itypeload));
  Multiplexer #(.width(2)) multiplexer_2 (.in0(2'b00), .in1(2'b10), .out(multiplexer_2_out), .sel(or_10_out));
  or or_10 (or_10_out, jal, jalr);
  or or_11 (or_11_out, Stype, SBtype);
  assign or_12_out = multiplexer_1_out | multiplexer_2_out;  // OR_Gate or_12, 2 bits wide
  not not_4 (RegWen, or_11_out);
  Multiplexer #(.select(2), .width(2)) multiplexer_3 (
    .in0(2'b01), .in1(2'b00), .in2(2'b10), .out(WBsel), .sel(or_12_out));  // open: in3
  Comparator #(.width(3)) comparator_40 (.a(3'b000), .b(instruction[14:12]), .eq(comparator_40_eq));  // open: gt, lt
  Comparator #(.width(3)) comparator_41 (.a(3'b001), .b(instruction[14:12]), .eq(comparator_41_eq));  // open: gt, lt
  Comparator #(.width(3)) comparator_42 (.a(3'b010), .b(instruction[14:12]), .eq(comparator_42_eq));  // open: gt, lt
  Comparator #(.width(3)) comparator_43 (.a(3'b000), .b(instruction[14:12]), .eq(comparator_43_eq));  // open: gt, lt
  Comparator #(.width(3)) comparator_44 (.a(3'b001), .b(instruction[14:12]), .eq(comparator_44_eq));  // open: gt, lt
  Comparator #(.width(7)) comparator_45 (.a({7{1'b0}}), .b(instruction[31:25]), .eq(comparator_45_eq));  // open: gt, lt
  Comparator #(.width(3)) comparator_46 (.a(3'b101), .b(instruction[14:12]), .eq(comparator_46_eq));  // open: gt, lt
  Comparator #(.width(7)) comparator_47 (.a({7{1'b0}}), .b(instruction[31:25]), .eq(comparator_47_eq));  // open: gt, lt
  Comparator #(.width(3)) comparator_48 (.a(3'b101), .b(instruction[14:12]), .eq(comparator_48_eq));  // open: gt, lt
  Comparator #(.width(7)) comparator_49 (
    .a(7'b0100000), .b(instruction[31:25]), .eq(comparator_49_eq));  // open: gt, lt
  Comparator #(.width(3)) comparator_50 (.a(3'b101), .b(instruction[14:12]), .eq(comparator_50_eq));  // open: gt, lt
  Comparator #(.width(3)) comparator_51 (.a(3'b110), .b(instruction[14:12]), .eq(comparator_51_eq));  // open: gt, lt
  Comparator #(.width(3)) comparator_52 (.a(3'b111), .b(instruction[14:12]), .eq(comparator_52_eq));  // open: gt, lt
  and and_25 (lb, comparator_40_eq, Itypeload);
  and and_26 (lh, comparator_41_eq, Itypeload);
  and and_27 (lw, comparator_42_eq, Itypeload);
  and and_28 (addi, comparator_43_eq, Itypeother);
  and and_29 (slli, comparator_44_eq, comparator_45_eq, Itypeother);
  and and_30 (srli, comparator_46_eq, comparator_47_eq, Itypeother);
  and and_31 (srai, comparator_48_eq, comparator_49_eq, Itypeother);
  and and_32 (bge, comparator_50_eq, SBtype);
  and and_33 (bltu, comparator_51_eq, SBtype);
  and and_34 (bgeu, comparator_52_eq, SBtype);
  or or_13 (or_13_out, Itypeload, jalr, Itypeother);
  or or_14 (Brun, bltu, bgeu);
  Multiplexer #(.width(3)) multiplexer_4 (.in0(3'b000), .in1(3'b001), .out(multiplexer_4_out), .sel(or_13_out));
  Multiplexer #(.width(3)) multiplexer_5 (.in0(3'b000), .in1(3'b010), .out(multiplexer_5_out), .sel(Stype));
  Multiplexer #(.width(3)) multiplexer_6 (.in0(3'b000), .in1(3'b011), .out(multiplexer_6_out), .sel(SBtype));
  Multiplexer #(.width(3)) multiplexer_7 (.in0(3'b000), .in1(3'b100), .out(multiplexer_7_out), .sel(or_15_out));
  or or_15 (or_15_out, auipc, lui);
  Multiplexer #(.width(3)) multiplexer_8 (.in0(3'b000), .in1(3'b101), .out(multiplexer_8_out), .sel(jal));
  Comparator #(.width(3)) comparator_53 (.a(3'b010), .b(instruction[14:12]), .eq(comparator_53_eq));  // open: gt, lt
  Comparator #(.width(3)) comparator_54 (.a(3'b100), .b(instruction[14:12]), .eq(comparator_54_eq));  // open: gt, lt
  Comparator #(.width(3)) comparator_55 (.a(3'b110), .b(instruction[14:12]), .eq(comparator_55_eq));  // open: gt, lt
  Comparator #(.width(3)) comparator_56 (.a(3'b111), .b(instruction[14:12]), .eq(comparator_56_eq));  // open: gt, lt
  or or_16 (MemRw, Stype, 1'b0);
  assign or_17_out = multiplexer_4_out | multiplexer_5_out | multiplexer_6_out | multiplexer_7_out | multiplexer_8_out;  // OR_Gate or_17, 3 bits wide
  and and_35 (slti, comparator_53_eq, Itypeother);
  and and_36 (xori, comparator_54_eq, Itypeother);
  and and_37 (ori, comparator_55_eq, Itypeother);
  and and_38 (andi, comparator_56_eq, Itypeother);
  assign IMMsel = 3'b000 | or_17_out;  // OR_Gate or_18, 3 bits wide
  Multiplexer #(.width(4)) multiplexer_9 (.in0(4'b0000), .in1(4'b0000), .out(multiplexer_9_out), .sel(add));
  Multiplexer #(.width(4)) multiplexer_10 (.in0(4'b0000), .in1(4'b1000), .out(multiplexer_10_out), .sel(mul));
  Multiplexer #(.width(4)) multiplexer_11 (.in0(4'b0000), .in1(4'b1100), .out(multiplexer_11_out), .sel(sub));
  Multiplexer #(.width(4)) multiplexer_12 (.in0(4'b0000), .in1(4'b0001), .out(multiplexer_12_out), .sel(sll1));
  Multiplexer #(.width(4)) multiplexer_13 (.in0(4'b0000), .in1(4'b1001), .out(multiplexer_13_out), .sel(mulh));
  Multiplexer #(.width(4)) multiplexer_14 (.in0(4'b0000), .in1(4'b1011), .out(multiplexer_14_out), .sel(mulhu));
  Multiplexer #(.width(4)) multiplexer_15 (.in0(4'b0000), .in1(4'b0010), .out(multiplexer_15_out), .sel(slt));
  Multiplexer #(.width(4)) multiplexer_16 (.in0(4'b0000), .in1(4'b0100), .out(multiplexer_16_out), .sel(xor1));
  Multiplexer #(.width(4)) multiplexer_17 (.in0(4'b0000), .in1(4'b0101), .out(multiplexer_17_out), .sel(srl1));
  Multiplexer #(.width(4)) multiplexer_18 (.in0(4'b0000), .in1(4'b1101), .out(multiplexer_18_out), .sel(sra1));
  Multiplexer #(.width(4)) multiplexer_19 (.in0(4'b0000), .in1(4'b0000), .out(multiplexer_19_out), .sel(lb));
  Multiplexer #(.width(4)) multiplexer_20 (.in0(4'b0000), .in1(4'b0000), .out(multiplexer_20_out), .sel(lh));
  Multiplexer #(.width(4)) multiplexer_21 (.in0(4'b0000), .in1(4'b0000), .out(multiplexer_21_out), .sel(lw));
  Multiplexer #(.width(4)) multiplexer_22 (.in0(4'b0000), .in1(4'b0000), .out(multiplexer_22_out), .sel(addi));
  Multiplexer #(.width(4)) multiplexer_23 (.in0(4'b0000), .in1(4'b0001), .out(multiplexer_23_out), .sel(slli));
  Multiplexer #(.width(4)) multiplexer_24 (.in0(4'b0000), .in1(4'b0010), .out(multiplexer_24_out), .sel(slti));
  Multiplexer #(.width(4)) multiplexer_25 (.in0(4'b0000), .in1(4'b0100), .out(multiplexer_25_out), .sel(xori));
  Multiplexer #(.width(4)) multiplexer_26 (.in0(4'b0000), .in1(4'b0101), .out(multiplexer_26_out), .sel(srli));
  Multiplexer #(.width(4)) multiplexer_27 (.in0(4'b0000), .in1(4'b1101), .out(multiplexer_27_out), .sel(srai));
  Multiplexer #(.width(4)) multiplexer_28 (.in0(4'b0000), .in1(4'b0110), .out(multiplexer_28_out), .sel(ori));
  Multiplexer #(.width(4)) multiplexer_29 (.in0(4'b0000), .in1(4'b0111), .out(multiplexer_29_out), .sel(andi));
  Multiplexer #(.width(4)) multiplexer_30 (.in0(4'b0000), .in1(4'b0000), .out(multiplexer_30_out), .sel(sb));
  Multiplexer #(.width(4)) multiplexer_31 (.in0(4'b0000), .in1(4'b0000), .out(multiplexer_31_out), .sel(sh));
  Multiplexer #(.width(4)) multiplexer_32 (.in0(4'b0000), .in1(4'b0000), .out(multiplexer_32_out), .sel(sw));
  Multiplexer #(.width(4)) multiplexer_33 (.in0(4'b0000), .in1(4'b0000), .out(multiplexer_33_out), .sel(beq));
  Multiplexer #(.width(4)) multiplexer_34 (.in0(4'b0000), .in1(4'b0000), .out(multiplexer_34_out), .sel(bne));
  Multiplexer #(.width(4)) multiplexer_35 (.in0(4'b0000), .in1(4'b0000), .out(multiplexer_35_out), .sel(blt));
  Multiplexer #(.width(4)) multiplexer_36 (.in0(4'b0000), .in1(4'b0000), .out(multiplexer_36_out), .sel(bge));
  Multiplexer #(.width(4)) multiplexer_37 (.in0(4'b0000), .in1(4'b0000), .out(multiplexer_37_out), .sel(bltu));
  Multiplexer #(.width(4)) multiplexer_38 (.in0(4'b0000), .in1(4'b0000), .out(multiplexer_38_out), .sel(bgeu));
  Multiplexer #(.width(4)) multiplexer_39 (.in0(4'b0000), .in1(4'b0000), .out(multiplexer_39_out), .sel(auipc));
  Multiplexer #(.width(4)) multiplexer_40 (.in0(4'b0000), .in1(4'b0000), .out(multiplexer_40_out), .sel(lui));
  Multiplexer #(.width(4)) multiplexer_41 (.in0(4'b0000), .in1(4'b0000), .out(multiplexer_41_out), .sel(jal));
  Multiplexer #(.width(4)) multiplexer_42 (.in0(4'b0000), .in1(4'b0000), .out(multiplexer_42_out), .sel(jalr));
  assign or_19_out = multiplexer_9_out | multiplexer_10_out;  // OR_Gate or_19, 4 bits wide
  assign or_20_out = multiplexer_11_out | multiplexer_12_out;  // OR_Gate or_20, 4 bits wide
  assign or_21_out = multiplexer_13_out | multiplexer_14_out;  // OR_Gate or_21, 4 bits wide
  assign or_22_out = multiplexer_15_out | multiplexer_16_out;  // OR_Gate or_22, 4 bits wide
  assign or_23_out = multiplexer_17_out | multiplexer_18_out;  // OR_Gate or_23, 4 bits wide
  assign or_24_out = multiplexer_19_out | multiplexer_20_out;  // OR_Gate or_24, 4 bits wide
  assign or_25_out = multiplexer_21_out | multiplexer_22_out;  // OR_Gate or_25, 4 bits wide
  assign or_26_out = multiplexer_23_out | multiplexer_24_out;  // OR_Gate or_26, 4 bits wide
  assign or_27_out = multiplexer_25_out | multiplexer_26_out;  // OR_Gate or_27, 4 bits wide
  assign or_28_out = multiplexer_27_out | multiplexer_28_out;  // OR_Gate or_28, 4 bits wide
  assign or_29_out = multiplexer_29_out | multiplexer_30_out;  // OR_Gate or_29, 4 bits wide
  assign or_30_out = multiplexer_31_out | multiplexer_32_out;  // OR_Gate or_30, 4 bits wide
  assign or_31_out = multiplexer_33_out | multiplexer_34_out;  // OR_Gate or_31, 4 bits wide
  assign or_32_out = multiplexer_35_out | multiplexer_36_out;  // OR_Gate or_32, 4 bits wide
  assign or_33_out = multiplexer_37_out | multiplexer_38_out;  // OR_Gate or_33, 4 bits wide
  assign or_34_out = multiplexer_39_out | multiplexer_40_out;  // OR_Gate or_34, 4 bits wide
  assign or_35_out = multiplexer_41_out | multiplexer_42_out;  // OR_Gate or_35, 4 bits wide
  assign or_36_out = or_19_out | or_20_out;  // OR_Gate or_36, 4 bits wide
  assign or_37_out = or_21_out | or_22_out;  // OR_Gate or_37, 4 bits wide
  assign or_38_out = or_23_out | or_24_out;  // OR_Gate or_38, 4 bits wide
  assign or_39_out = or_25_out | or_26_out;  // OR_Gate or_39, 4 bits wide
  assign or_40_out = or_27_out | or_28_out;  // OR_Gate or_40, 4 bits wide
  assign or_41_out = or_29_out | or_30_out;  // OR_Gate or_41, 4 bits wide
  assign or_42_out = or_31_out | or_32_out;  // OR_Gate or_42, 4 bits wide
  assign or_43_out = or_33_out | or_34_out;  // OR_Gate or_43, 4 bits wide
  assign or_44_out = or_36_out | or_37_out | or_38_out;  // OR_Gate or_44, 4 bits wide
  assign or_45_out = or_39_out | or_40_out | or_41_out;  // OR_Gate or_45, 4 bits wide
  assign or_46_out = or_42_out | or_43_out | or_35_out;  // OR_Gate or_46, 4 bits wide
  assign ALUsel = or_44_out | or_45_out | or_46_out;  // OR_Gate or_47, 4 bits wide

  assign PCsel = flush;

  // Other names for the same wires on the sheet: opcode[6:0] = instruction[6:0]; func3[2:0] = instruction[14:12];
  //   func7[6:0] = instruction[31:25]
endmodule

module branchcomp (
  input  [31:0] rs1,
  input  [31:0] rs2,
  input  BrUn,
  output BrEq,
  output BrLt
);

  wire comparator_1_lt, comparator_2_lt;

  Comparator #(.width(32)) comparator_1 (.a(rs1), .b(rs2), .eq(BrEq), .lt(comparator_1_lt));  // open: gt
  Comparator #(.mode("unsigned"), .width(32)) comparator_2 (.a(rs1), .b(rs2), .lt(comparator_2_lt));  // open: gt, eq
  Multiplexer multiplexer_1 (.in0(comparator_1_lt), .in1(comparator_2_lt), .out(BrLt), .sel(BrUn));
endmodule

module add (
  input  A,
  input  B,
  input  C,
  output S,
  output Cout
);

  wire and_1_out, and_2_out, and_3_out, xor_1_out;

  and and_1 (and_1_out, B, C);
  and and_2 (and_2_out, A, B);
  and and_3 (and_3_out, A, C);
  xor xor_1 (xor_1_out, A, B);
  or or_1 (Cout, and_2_out, and_3_out, and_1_out);
  xor xor_2 (S, xor_1_out, C);
endmodule
